# Fritzing sketch L298WithWindSensorPinout (saved by Fritzing 1.0.6)
breadboards: 1

parts:
  Sensor1 = Wind Sensor rev C4 [part_number=MD0550]
  Driver1 = 28BYJ-48 Driver Module [part_number=ULN2003 package=THT]
  M1 = STM32F103C8T6 blue mini board
  Part1 = Adafruit MPM3610 5V
  U1 = rectifier sql50A
  Part2 = Adafruit INA169 Analog DC Current Sensor Breakout [part_number="Adafruit #1164"]
  A1 = DYS BE1806

nets:
  GND: Sensor1.GND, Part2.GND
  N1: Sensor1.+V, Part2.VCC
  N2: Sensor1.RV, M1.A1
  N3: Sensor1.TMP, M1.A0
  N4: Driver1.IN1, M1.B9
  N5: Driver1.IN2, M1.B8
  N6: Driver1.IN3, M1.B7
  N7: Driver1.IN4, M1.B6
  N8: M1.G, Part1.5.0V, Part1.GND
  N9: Part1.EN, Part2.OUT
  N10: Part1.VIN, U1.Pin_5
  N11: U1.Pin_1, A1.Pin_3
  N12: U1.Pin_2, A1.Pin_1
  N13: U1.Pin_3, Part2.VIN-
  N14: U1.Pin_4, Part2.VIN+, A1.Pin_2

notes:
  Rectifier is simplified, may need separate power for current sensor

custom parts:
  Wind Sensor rev C4: Modern Device Thermal Anemometer rev. C4
  28BYJ-48 Driver Module: Generic male header
  rectifier sql50A: Reinder bridge 3 phase SQL50A 1000V.
  Adafruit INA169 Analog DC Current Sensor Breakout: This breakout board will solve all your current-monitoring problems. Instead of struggling with a multimeter, you can just use the handy INA169 chip on this breakout to both measure both the DC current draw and have a handy analog output that is with respect to ground. The analog output makes this an ideal breakout for feedback-loop control. Most current-measuring devices such as our current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
  DYS BE1806: quadcopter brushless motor.

// code stored in the sketch: L298WithWindSensor.ino
#define analogPinForRV A1
#define analogPinForTMP A0
#include <Stepper.h>

// to calibrate your sensor, put a glass over it, but the sensor should not be
// touching the desktop surface however.
// adjust the zeroWindAdjustment until your sensor reads about zero with the glass over it. 

const float zeroWindAdjustment = 0.2; // negative numbers yield smaller wind speeds and vice versa.

// wind speed module variables 
int TMP_Therm_ADunits;
float RV_Wind_ADunits;
float RV_Wind_Volts;
unsigned long lastMillis;
int TempCtimes100;
float zeroWind_ADunits;
float zeroWind_volts;
float WindSpeed_MPH;

const int stepsPerRevolution = 2048;
Stepper myStepper(stepsPerRevolution, 6, 7, 8, 9); // IN1-IN3-IN2-IN4

const float stepAngle = 360.0 / stepsPerRevolution;  
const int stepsFor30deg = (int)(30.0 / stepAngle);   // 171ish steps for 30°
bool turnedIn = false;  // track whether stepper is turned in

void setup() {
  Serial.begin(57600);
  Serial.println("Start: Wind sensor + stepper control");

  // optional: reset analog pins used by sensor
  pinMode(A2, INPUT);
  pinMode(A3, INPUT);
  digitalWrite(A3, LOW);

  myStepper.setSpeed(10); // RPM
}

void loop() {
  // read sensors every 0.5 seconds
  if (millis() - lastMillis > 500) {
    TMP_Therm_ADunits = analogRead(analogPinForTMP);
    RV_Wind_ADunits = analogRead(analogPinForRV);
    RV_Wind_Volts = RV_Wind_ADunits * 0.0048828125;

    // wind sensor calculations 
    TempCtimes100 = (0.005 * (float)TMP_Therm_ADunits * TMP_Therm_ADunits) - (16.862 * (float)TMP_Therm_ADunits) + 9075.4;
    zeroWind_ADunits = -0.0006 * ((float)TMP_Therm_ADunits * TMP_Therm_ADunits) + 1.0727 * (float)TMP_Therm_ADunits + 47.172;
    zeroWind_volts = (zeroWind_ADunits * 0.0048828125) - zeroWindAdjustment;
    WindSpeed_MPH = pow(((RV_Wind_Volts - zeroWind_volts) / 0.2300), 2.7265);

    Serial.print("WindSpeed (MPH): ");
    Serial.println(WindSpeed_MPH);
    float WindSpeed_MS = WindSpeed_MPH * 0.44704; // m/s

    // if wind >= 1 m/s, rotate stepper 30° inward. need to change angle depending on mech team needs?
    // what would the angle need to be to completely feather/stop the blade from turning?
    if (WindSpeed_MS >= 1.0 && !turnedIn) {
      Serial.println("Wind >= 1 m/s, turning");
      myStepper.setSpeed(10);
      myStepper.step(stepsFor30deg);
      turnedIn = true;
    } 
    // if wind drops below 1 m/s, return to original position
    else if (WindSpeed_MS < 1.0 && turnedIn) {
      Serial.println("Wind < 1 m/s, returning to original position");
      myStepper.setSpeed(10);
      myStepper.step(-stepsFor30deg);
      turnedIn = false;
    }

    lastMillis = millis();
  }
}
